// Logisim project TALLER_LOGICA_DIGITAL.circ as structural Verilog: 21 circuits, main circuit Full Adder - 1 bit
module Full_Adder___1_bit (
  input  A,
  input  B,
  input  Cin,
  output S,
  output C
);

  wire and_1_out, and_2_out, xor_1_out;

  xor xor_1 (xor_1_out, A, B);
  and and_1 (and_1_out, xor_1_out, Cin);
  and and_2 (and_2_out, A, B);
  xor xor_2 (S, xor_1_out, Cin);
  or or_1 (C, and_1_out, and_2_out);
endmodule

module Full_Adder___4_bits (
  input  [3:0] A,
  input  [3:0] B,
  input  Cin,
  output S3,
  output S2,
  output S1,
  output S0,
  output C
);

  wire full_adder_1_bit_1_c, full_adder_1_bit_2_c, full_adder_1_bit_3_c;

  Full_Adder___1_bit full_adder_1_bit_1 (.A(A[0]), .B(B[0]), .Cin(Cin), .S(S0), .C(full_adder_1_bit_1_c));
  Full_Adder___1_bit full_adder_1_bit_2 (
    .A(A[1]), .B(B[1]), .Cin(full_adder_1_bit_1_c), .S(S1), .C(full_adder_1_bit_2_c));
  Full_Adder___1_bit full_adder_1_bit_3 (
    .A(A[2]), .B(B[2]), .Cin(full_adder_1_bit_2_c), .S(S2), .C(full_adder_1_bit_3_c));
  Full_Adder___1_bit full_adder_1_bit_4 (.A(A[3]), .B(B[3]), .Cin(full_adder_1_bit_3_c), .S(S3), .C(C));
endmodule

module Full_Adder___4_bits_c__flags (
  input  [3:0] A,
  input  [3:0] B,
  input  Cin,
  output S3,
  output S2,
  output S1,
  output S0,
  output C,
  output N,
  output V,
  output Z
);

  wire and_1_out, and_2_out, not_1_out, not_2_out, not_3_out;

  Full_Adder___4_bits FULL_ADDER_4_BITS (.A(A), .B(B), .Cin(Cin), .S3(N), .S2(S2), .S1(S1), .S0(S0), .C(C));
  Zero zero_1 (.B3(N), .B2(S2), .B1(S1), .B0(S0), .out_5(Z));
  not not_1 (not_1_out, A[3]);
  not not_2 (not_2_out, B[3]);
  not not_3 (not_3_out, N);
  and and_1 (and_1_out, not_1_out, not_2_out, N);
  and and_2 (and_2_out, A[3], B[3], not_3_out);
  or or_1 (V, and_1_out, and_2_out);

  assign S3 = N;
endmodule

module Restador___4_bits (
  input  [3:0] A,
  input  [3:0] B,
  output S3,
  output S2,
  output S1,
  output S0,
  output C
);

  wire [3:0] not_1_out;

  assign not_1_out = ~B;  // NOT_Gate not_1, 4 bits wide
  Full_Adder___4_bits full_adder_4_bits_1 (.A(A), .B(not_1_out), .Cin(1'b1), .S3(S3), .S2(S2), .S1(S1), .S0(S0), .C(C));
endmodule

module Restador___4_bits_c__flags (
  input  [3:0] A,
  input  [3:0] B,
  output S3,
  output S2,
  output S1,
  output S0,
  output C,
  output N,
  output V,
  output Z
);

  wire and_1_out, and_2_out, not_1_out, not_2_out, not_3_out, not_4_out, not_5_out;

  Restador___4_bits RESTADOR_4_BITS (.A(A), .B(B), .S3(N), .S2(S2), .S1(S1), .S0(S0));  // open: C
  Zero zero_1 (.B3(N), .B2(S2), .B1(S1), .B0(S0), .out_5(Z));
  not not_1 (not_1_out, B[3]);
  not not_2 (not_2_out, N);
  not not_3 (not_3_out, A[3]);
  not not_4 (not_4_out, A[3]);
  not not_5 (not_5_out, B[3]);
  and and_1 (and_1_out, not_1_out, not_2_out, A[3]);
  and and_2 (and_2_out, B[3], N, not_3_out);
  and and_3 (C, not_4_out, not_5_out, N);
  or or_1 (V, and_1_out, and_2_out);

  assign S3 = N;
endmodule

module AND___4_bits_c__flags (
  input  [3:0] A,
  input  [3:0] B,
  output S3,
  output S2,
  output S1,
  output S0,
  output C,
  output N,
  output V,
  output Z
);

  and and_1 (S0, B[0], A[0]);
  and and_2 (S1, B[1], A[1]);
  and and_3 (S2, B[2], A[2]);
  and and_4 (N, B[3], A[3]);
  Zero zero_1 (.B3(N), .B2(S2), .B1(S1), .B0(S0), .out_5(Z));

  assign C = 1'b0;
  assign S3 = N;
  assign V = 1'b0;
endmodule

module OR___4_bits_c__flags (
  input  [3:0] A,
  input  [3:0] B,
  output S3,
  output S2,
  output S1,
  output S0,
  output C,
  output N,
  output V,
  output Z
);

  or or_1 (S0, B[0], A[0]);
  or or_2 (S1, B[1], A[1]);
  or or_3 (S2, B[2], A[2]);
  or or_4 (N, B[3], A[3]);
  Zero zero_1 (.B3(N), .B2(S2), .B1(S1), .B0(S0), .out_5(Z));

  assign C = 1'b0;
  assign S3 = N;
  assign V = 1'b0;
endmodule

module EJ4___ALU___4_bits_c__flags (
  input  [3:0] A,
  input  [3:0] B,
  input  [1:0] OP,
  output [3:0] S,
  output C,
  output N,
  output V,
  output Z
);

  wire [3:0] and_4_bits_c_flags_1_s0, and_4_bits_c_flags_1_z, full_adder_4_bits_c_flags_1_s0,
       full_adder_4_bits_c_flags_1_z, or_4_bits_c_flags_1_s0, or_4_bits_c_flags_1_z,
       restador_4_bits_c_flags_1_s0, restador_4_bits_c_flags_1_z;

  Full_Adder___4_bits_c__flags full_adder_4_bits_c_flags_1 (
    .A(A), .B(B), .Cin(1'b0), .S3(full_adder_4_bits_c_flags_1_s0[3]), .S2(full_adder_4_bits_c_flags_1_s0[2]),
    .S1(full_adder_4_bits_c_flags_1_s0[1]), .S0(full_adder_4_bits_c_flags_1_s0[0]),
    .C(full_adder_4_bits_c_flags_1_z[3]), .N(full_adder_4_bits_c_flags_1_z[2]),
    .V(full_adder_4_bits_c_flags_1_z[1]), .Z(full_adder_4_bits_c_flags_1_z[0]));
  Restador___4_bits_c__flags restador_4_bits_c_flags_1 (
    .A(A), .B(B), .S3(restador_4_bits_c_flags_1_s0[3]), .S2(restador_4_bits_c_flags_1_s0[2]),
    .S1(restador_4_bits_c_flags_1_s0[1]), .S0(restador_4_bits_c_flags_1_s0[0]),
    .C(restador_4_bits_c_flags_1_z[3]), .N(restador_4_bits_c_flags_1_z[2]),
    .V(restador_4_bits_c_flags_1_z[1]), .Z(restador_4_bits_c_flags_1_z[0]));
  AND___4_bits_c__flags and_4_bits_c_flags_1 (
    .A(A), .B(B), .S3(and_4_bits_c_flags_1_s0[3]), .S2(and_4_bits_c_flags_1_s0[2]),
    .S1(and_4_bits_c_flags_1_s0[1]), .S0(and_4_bits_c_flags_1_s0[0]), .C(and_4_bits_c_flags_1_z[3]),
    .N(and_4_bits_c_flags_1_z[2]), .V(and_4_bits_c_flags_1_z[1]), .Z(and_4_bits_c_flags_1_z[0]));
  OR___4_bits_c__flags or_4_bits_c_flags_1 (
    .A(A), .B(B), .S3(or_4_bits_c_flags_1_s0[3]), .S2(or_4_bits_c_flags_1_s0[2]),
    .S1(or_4_bits_c_flags_1_s0[1]), .S0(or_4_bits_c_flags_1_s0[0]), .C(or_4_bits_c_flags_1_z[3]),
    .N(or_4_bits_c_flags_1_z[2]), .V(or_4_bits_c_flags_1_z[1]), .Z(or_4_bits_c_flags_1_z[0]));
  Multiplexer #(.select(2), .width(4)) multiplexer_1 (
    .in0(full_adder_4_bits_c_flags_1_s0), .in1(restador_4_bits_c_flags_1_s0), .in2(and_4_bits_c_flags_1_s0),
    .in3(or_4_bits_c_flags_1_s0), .out(S), .sel(OP));  // open: en
  Multiplexer #(.select(2), .width(4)) multiplexer_2 (
    .in0(full_adder_4_bits_c_flags_1_z), .in1(restador_4_bits_c_flags_1_z), .in2(and_4_bits_c_flags_1_z),
    .in3(or_4_bits_c_flags_1_z), .out({C, N, V, Z}), .sel(OP));  // open: en

  // Notes on the sheet:
  //   ALU 4 BITS
endmodule

module Zero (
  input  B3,
  input  B2,
  input  B1,
  input  B0,
  output out_5
);

  nor nor_1 (out_5, B3, B2, B1, B0);
endmodule

module registro_salida_restringida (
  input  clk,
  input  in,
  input  w,
  input  en_out,
  output out_debug,
  output out
);

  D_Flip_Flop d_ff_1 (.clk(clk), .D(in), .Q(out_debug), .en(w));  // open: Qn, preset, reset
  assign out = en_out ? out_debug : 1'bz;  // Controlled_Buffer controlled_buffer_1
endmodule

module Registro_Simple___4_bits (
  input  [3:0] I,
  input  LOAD,
  input  CLK,
  output O3,
  output O2,
  output O1,
  output O0
);

  wire and_1_out, and_2_out, and_3_out, and_4_out, and_5_out, and_6_out, and_7_out, and_8_out, not_1_out,
       not_2_out, not_3_out, not_4_out, or_1_out, or_2_out, or_3_out, or_4_out;

  not not_1 (not_1_out, LOAD);
  not not_2 (not_2_out, LOAD);
  not not_3 (not_3_out, LOAD);
  not not_4 (not_4_out, LOAD);
  and and_1 (and_1_out, LOAD, I[0]);
  and and_2 (and_2_out, not_1_out, O0);
  and and_3 (and_3_out, LOAD, I[1]);
  and and_4 (and_4_out, not_2_out, O1);
  and and_5 (and_5_out, LOAD, I[2]);
  and and_6 (and_6_out, not_3_out, O2);
  and and_7 (and_7_out, LOAD, I[3]);
  and and_8 (and_8_out, not_4_out, O3);
  or or_1 (or_1_out, and_1_out, and_2_out);
  or or_2 (or_2_out, and_3_out, and_4_out);
  or or_3 (or_3_out, and_5_out, and_6_out);
  or or_4 (or_4_out, and_7_out, and_8_out);
  D_Flip_Flop d_ff_1 (.clk(CLK), .D(or_1_out), .Q(O0));  // open: Qn, preset, en, reset
  D_Flip_Flop d_ff_2 (.clk(CLK), .D(or_2_out), .Q(O1));  // open: Qn, preset, en, reset
  D_Flip_Flop d_ff_3 (.clk(CLK), .D(or_3_out), .Q(O2));  // open: Qn, preset, en, reset
  D_Flip_Flop d_ff_4 (.clk(CLK), .D(or_4_out), .Q(O3));  // open: Qn, preset, en, reset
endmodule

module Registro_Simple___4_bits_V2 (
  input  [3:0] I,
  input  LOAD,
  input  CLK,
  output O3,
  output O2,
  output O1,
  output O0
);

  D_Flip_Flop d_ff_1 (.clk(CLK), .D(I[0]), .Q(O0), .en(LOAD));  // open: Qn, preset, reset
  D_Flip_Flop d_ff_2 (.clk(CLK), .D(I[1]), .Q(O1), .en(LOAD));  // open: Qn, preset, reset
  D_Flip_Flop d_ff_3 (.clk(CLK), .D(I[2]), .Q(O2), .en(LOAD));  // open: Qn, preset, reset
  D_Flip_Flop d_ff_4 (.clk(CLK), .D(I[3]), .Q(O3), .en(LOAD));  // open: Qn, preset, reset
endmodule

module Registro_Salida_Restringida___4_bits (
  input  [3:0] I,
  input  LOAD,
  input  CLK,
  input  READ,
  output O3,
  output O2,
  output O1,
  output O0
);

  wire d_ff_1_q, registro_simple_4_bits_1_o0, registro_simple_4_bits_1_o1, registro_simple_4_bits_1_o2,
       registro_simple_4_bits_1_o3;

  Registro_Simple___4_bits registro_simple_4_bits_1 (
    .I(I), .LOAD(LOAD), .CLK(CLK), .O3(registro_simple_4_bits_1_o3), .O2(registro_simple_4_bits_1_o2),
    .O1(registro_simple_4_bits_1_o1), .O0(registro_simple_4_bits_1_o0));
  D_Flip_Flop d_ff_1 (.clk(CLK), .D(READ), .Q(d_ff_1_q));  // open: Qn, preset, en, reset
  assign O3 = d_ff_1_q ? registro_simple_4_bits_1_o3 : 1'bz;  // Controlled_Buffer controlled_buffer_1
  assign O2 = d_ff_1_q ? registro_simple_4_bits_1_o2 : 1'bz;  // Controlled_Buffer controlled_buffer_2
  assign O1 = d_ff_1_q ? registro_simple_4_bits_1_o1 : 1'bz;  // Controlled_Buffer controlled_buffer_3
  assign O0 = d_ff_1_q ? registro_simple_4_bits_1_o0 : 1'bz;  // Controlled_Buffer controlled_buffer_4
endmodule

module EJ1___Contador_de_unos____4_bits (
  input  [3:0] A,
  output [2:0] S
);

  wire full_adder_1_bit_1_c, full_adder_1_bit_1_s, full_adder_1_bit_2_c, full_adder_1_bit_2_s,
       full_adder_1_bit_3_c;

  Full_Adder___1_bit full_adder_1_bit_1 (
    .A(A[0]), .B(A[1]), .Cin(1'b0), .S(full_adder_1_bit_1_s), .C(full_adder_1_bit_1_c));
  Full_Adder___1_bit full_adder_1_bit_2 (
    .A(A[2]), .B(A[3]), .Cin(1'b0), .S(full_adder_1_bit_2_s), .C(full_adder_1_bit_2_c));
  Full_Adder___1_bit full_adder_1_bit_3 (
    .A(full_adder_1_bit_2_s), .B(full_adder_1_bit_1_s), .Cin(1'b0), .S(S[0]), .C(full_adder_1_bit_3_c));
  Full_Adder___1_bit full_adder_1_bit_4 (
    .A(full_adder_1_bit_1_c), .B(full_adder_1_bit_2_c), .Cin(full_adder_1_bit_3_c), .S(S[1]), .C(S[2]));
endmodule

module EJ2___Incrementador___4_bits (
  input  [3:0] A,
  output [3:0] S
);

  wire and_1_out, and_2_out, not_2_out, not_3_out;

  not not_1 (S[0], A[0]);
  xor xor_1 (S[1], A[0], A[1]);
  not not_2 (not_2_out, S[1]);
  and and_1 (and_1_out, A[1], not_2_out);
  not not_3 (not_3_out, S[2]);
  xor xor_2 (S[2], and_1_out, A[2]);
  and and_2 (and_2_out, not_3_out, A[2]);
  xor xor_3 (S[3], and_2_out, A[3]);
endmodule

module EJ3___Sumador___4_bits_c__flags (
  input  [3:0] A,
  input  [3:0] B,
  input  Cin,
  output [3:0] S,
  output Z,
  output C,
  output V,
  output N,
  output Cout
);

  wire and_1_out, and_2_out, full_adder_1_bit_1_c, full_adder_1_bit_2_c, full_adder_1_bit_3_c, not_1_out,
       not_2_out, not_3_out, not_4_out, not_5_out, not_6_out, not_7_out;

  Full_Adder___1_bit full_adder_1_bit_1 (.A(A[0]), .B(B[0]), .Cin(Cin), .S(S[0]), .C(full_adder_1_bit_1_c));
  Full_Adder___1_bit full_adder_1_bit_2 (
    .A(A[1]), .B(B[1]), .Cin(full_adder_1_bit_1_c), .S(S[1]), .C(full_adder_1_bit_2_c));
  Full_Adder___1_bit full_adder_1_bit_3 (
    .A(A[2]), .B(B[2]), .Cin(full_adder_1_bit_2_c), .S(S[2]), .C(full_adder_1_bit_3_c));
  Full_Adder___1_bit full_adder_1_bit_4 (.A(A[3]), .B(B[3]), .Cin(full_adder_1_bit_3_c), .S(N), .C(C));
  not not_1 (not_1_out, S[0]);
  not not_2 (not_2_out, S[1]);
  not not_3 (not_3_out, S[2]);
  not not_4 (not_4_out, N);
  not not_5 (not_5_out, A[3]);
  not not_6 (not_6_out, B[3]);
  not not_7 (not_7_out, N);
  and and_1 (and_1_out, not_5_out, not_6_out, N);
  and and_2 (and_2_out, A[3], B[3], not_7_out);
  and and_3 (Z, not_1_out, not_2_out, not_3_out, not_4_out);
  or or_1 (V, and_1_out, and_2_out, C);

  assign Cout = C;
  assign S[3] = N;
endmodule

module EJ4___ALU (
  input  [3:0] A,
  input  [3:0] B,
  input  [1:0] OP,
  output [3:0] S,
  output C,
  output N,
  output V,
  output Z
);

  wire [3:0] and_4_bits_c_flags_1_s0, and_4_bits_c_flags_1_z, full_adder_4_bits_c_flags_1_s0,
       full_adder_4_bits_c_flags_1_z, or_4_bits_c_flags_1_s0, or_4_bits_c_flags_1_z,
       restador_4_bits_c_flags_1_s0, restador_4_bits_c_flags_1_z;

  Full_Adder___4_bits_c__flags full_adder_4_bits_c_flags_1 (
    .A(A), .B(B), .Cin(1'b0), .S3(full_adder_4_bits_c_flags_1_s0[3]), .S2(full_adder_4_bits_c_flags_1_s0[2]),
    .S1(full_adder_4_bits_c_flags_1_s0[1]), .S0(full_adder_4_bits_c_flags_1_s0[0]),
    .C(full_adder_4_bits_c_flags_1_z[3]), .N(full_adder_4_bits_c_flags_1_z[2]),
    .V(full_adder_4_bits_c_flags_1_z[1]), .Z(full_adder_4_bits_c_flags_1_z[0]));
  Restador___4_bits_c__flags restador_4_bits_c_flags_1 (
    .A(A), .B(B), .S3(restador_4_bits_c_flags_1_s0[3]), .S2(restador_4_bits_c_flags_1_s0[2]),
    .S1(restador_4_bits_c_flags_1_s0[1]), .S0(restador_4_bits_c_flags_1_s0[0]),
    .C(restador_4_bits_c_flags_1_z[3]), .N(restador_4_bits_c_flags_1_z[2]),
    .V(restador_4_bits_c_flags_1_z[1]), .Z(restador_4_bits_c_flags_1_z[0]));
  AND___4_bits_c__flags and_4_bits_c_flags_1 (
    .A(A), .B(B), .S3(and_4_bits_c_flags_1_s0[3]), .S2(and_4_bits_c_flags_1_s0[2]),
    .S1(and_4_bits_c_flags_1_s0[1]), .S0(and_4_bits_c_flags_1_s0[0]), .C(and_4_bits_c_flags_1_z[3]),
    .N(and_4_bits_c_flags_1_z[2]), .V(and_4_bits_c_flags_1_z[1]), .Z(and_4_bits_c_flags_1_z[0]));
  OR___4_bits_c__flags or_4_bits_c_flags_1 (
    .A(A), .B(B), .S3(or_4_bits_c_flags_1_s0[3]), .S2(or_4_bits_c_flags_1_s0[2]),
    .S1(or_4_bits_c_flags_1_s0[1]), .S0(or_4_bits_c_flags_1_s0[0]), .C(or_4_bits_c_flags_1_z[3]),
    .N(or_4_bits_c_flags_1_z[2]), .V(or_4_bits_c_flags_1_z[1]), .Z(or_4_bits_c_flags_1_z[0]));
  Multiplexer #(.select(2), .width(4)) multiplexer_1 (
    .in0(full_adder_4_bits_c_flags_1_s0), .in1(restador_4_bits_c_flags_1_s0), .in2(and_4_bits_c_flags_1_s0),
    .in3(or_4_bits_c_flags_1_s0), .out(S), .sel(OP));  // open: en
  Multiplexer #(.select(2), .width(4)) multiplexer_2 (
    .in0(full_adder_4_bits_c_flags_1_z), .in1(restador_4_bits_c_flags_1_z), .in2(and_4_bits_c_flags_1_z),
    .in3(or_4_bits_c_flags_1_z), .out({C, N, V, Z}), .sel(OP));  // open: en

  // Notes on the sheet:
  //   ALU 4 BITS
endmodule

module EJ5___Medio_compartido (
  input  en_A,
  input  A,
  input  B,
  input  en_B,
  output R
);

  assign R = en_A ? A : 1'bz;  // Controlled_Buffer controlled_buffer_1
  assign R = en_B ? B : 1'bz;  // Controlled_Buffer controlled_buffer_2

  // Notes on the sheet:
  //   EJERCICIO 5 - Componente medio compartido
endmodule

module EJ6___Movimiento_entre_registros (
  input  Force_input,
  input  en_force_input,
  input  w0,
  input  en0,
  input  w1,
  input  en1,
  input  w2,
  input  en2,
  input  clk,
  output BUS
);

  wire registro_salida_restringida_1_out_debug, registro_salida_restringida_2_out_debug,
       registro_salida_restringida_3_out_debug;

  assign BUS = en_force_input ? Force_input : 1'bz;  // Controlled_Buffer controlled_buffer_1
  registro_salida_restringida registro_salida_restringida_1 (
    .clk(clk), .in(BUS), .out_debug(registro_salida_restringida_1_out_debug), .out(BUS), .w(w0), .en_out(en0));
  // Probe on registro_salida_restringida_1_out_debug
  registro_salida_restringida registro_salida_restringida_2 (
    .clk(clk), .in(BUS), .out_debug(registro_salida_restringida_2_out_debug), .out(BUS), .w(w1), .en_out(en1));
  // Probe on registro_salida_restringida_2_out_debug
  registro_salida_restringida registro_salida_restringida_3 (
    .clk(clk), .in(BUS), .out_debug(registro_salida_restringida_3_out_debug), .out(BUS), .w(w2), .en_out(en2));
  // Probe on registro_salida_restringida_3_out_debug

  // Notes on the sheet:
  //   EJERCICIO 6 - Movimientos entre registros
endmodule

module registro_4b_salida_restringida (
  input  [3:0] In_4,
  input  clk,
  input  w,
  input  en_out,
  output [3:0] out4_d,
  output [3:0] out
);

  registro_salida_restringida registro_salida_restringida_1 (
    .clk(clk), .in(In_4[0]), .out_debug(out4_d[0]), .out(out[0]), .w(w), .en_out(en_out));
  registro_salida_restringida registro_salida_restringida_2 (
    .clk(clk), .in(In_4[1]), .out_debug(out4_d[1]), .out(out[1]), .w(w), .en_out(en_out));
  registro_salida_restringida registro_salida_restringida_3 (
    .clk(clk), .in(In_4[2]), .out_debug(out4_d[2]), .out(out[2]), .w(w), .en_out(en_out));
  registro_salida_restringida registro_salida_restringida_4 (
    .clk(clk), .in(In_4[3]), .out_debug(out4_d[3]), .out(out[3]), .w(w), .en_out(en_out));

  // Notes on the sheet:
  //   Registro 4b salida restringida
endmodule

module EJ7___Maquina_4_bits (
  input  wA,
  input  en0,
  input  w0,
  input  enS,
  input  wB,
  input  en1,
  input  [1:0] op,
  input  w1,
  input  en2,
  input  w2,
  input  en3,
  input  [3:0] Force_input,
  input  w3,
  input  clk,
  input  en_force_input,
  output C,
  output N,
  output V,
  output Z
);

  wire button_1_out, clk_t, not_1_out;
  wire [3:0] A, A_out, B, B_out, ej4_alu_1_s, R0_out, R0_out4_d, R1_out4_d, R2_out4_d, R3_out4_d, S;

  Hex_Digit_Display hex_digit_display_1 (.value(R0_out4_d));  // open: dp
  registro_4b_salida_restringida R0 (
    .In_4(R0_out), .clk(clk_t), .w(w0), .en_out(en0), .out4_d(R0_out4_d), .out(R0_out));
  Hex_Digit_Display hex_digit_display_2 (.value(R1_out4_d));  // open: dp
  registro_4b_salida_restringida R1 (
    .In_4(R0_out), .clk(clk_t), .w(w1), .en_out(en1), .out4_d(R1_out4_d), .out(R0_out));
  Hex_Digit_Display hex_digit_display_3 (.value(R2_out4_d));  // open: dp
  registro_4b_salida_restringida R2 (
    .In_4(R0_out), .clk(clk_t), .w(w2), .en_out(en2), .out4_d(R2_out4_d), .out(R0_out));
  Hex_Digit_Display hex_digit_display_4 (.value(R3_out4_d));  // open: dp
  registro_4b_salida_restringida R3 (
    .In_4(R0_out), .clk(clk_t), .w(w3), .en_out(en3), .out4_d(R3_out4_d), .out(R0_out));
  Hex_Digit_Display hex_digit_display_5 (.value(Force_input));  // open: dp
  assign R0_out = en_force_input ? Force_input : 4'bz;  // Controlled_Buffer controlled_buffer_1
  Hex_Digit_Display hex_digit_display_6 (.value(R0_out));  // open: dp
  registro_4b_salida_restringida u_A (.In_4(R0_out), .clk(clk_t), .w(wA), .en_out(1'b1), .out4_d(A), .out(A_out));
  registro_4b_salida_restringida u_B (.In_4(R0_out), .clk(clk_t), .w(wB), .en_out(1'b1), .out4_d(B), .out(B_out));
  Button button_1 (.out(button_1_out));
  Hex_Digit_Display hex_digit_display_7 (.value(A));  // open: dp
  or or_1 (clk_t, button_1_out, clk);
  Hex_Digit_Display hex_digit_display_8 (.value(B));  // open: dp
  EJ4___ALU ej4_alu_1 (.A(A_out), .B(B_out), .OP(op), .S(ej4_alu_1_s), .C(C), .N(N), .V(V), .Z(Z));
  Hex_Digit_Display hex_digit_display_9 (.value(S));  // open: dp
  not not_1 (not_1_out, clk_t);
  registro_4b_salida_restringida u_S (
    .In_4(ej4_alu_1_s), .clk(not_1_out), .w(1'b1), .en_out(enS), .out4_d(S), .out(R0_out));

  // Notes on the sheet:
  //   EJERCICIO 7 - Máquina de 4 bits
  //   BUS
  //   =
endmodule
