// Logisim project tallerLogicaDigital.circ as structural Verilog: 9 circuits, main circuit EJ1 - Contador Unos
module EJ1___Contador_Unos (
  input  [3:0] A,
  output [2:0] S
);


  // Notes on the sheet:
  //   EJERCICIO 1 - Contador de unos de 4 bits
endmodule

module EJ2___Incrementador (
  input  [3:0] A,
  output [3:0] S
);


  // Notes on the sheet:
  //   EJERCICIO 2 - Incrementador de 4 bits
endmodule

module EJ3___Sumador (
  input  [3:0] A,
  input  [3:0] B,
  input  Cin,
  output V,
  output N,
  output C,
  output Z,
  output [3:0] S,
  output Cout
);


  // Other names for the same wires on the sheet: carry = C; negative = N; overflow = V; zero = Z

  // Notes on the sheet:
  //   EJERCICIO 3 - Sumador de 4 bits con Flags ZCVN.
endmodule

// ALU
module EJ4___ALU (
  input  [1:0] OP,
  input  [3:0] A,
  input  [3:0] B,
  output V,
  output N,
  output C,
  output Z,
  output [3:0] S
);


  // Other names for the same wires on the sheet: carry = C; negative = N; overflow = V; zero = Z

  // Notes on the sheet:
  //   EJERCICIO 4 - ALU de 4 bits
endmodule

module EJ5___Medio_compartido (
  input  en_A,
  input  A,
  input  B,
  input  en_B,
  output R
);

  assign R = en_A ? A : 1'bz;  // Controlled_Buffer controlled_buffer_1
  assign R = en_B ? B : 1'bz;  // Controlled_Buffer controlled_buffer_2

  // Notes on the sheet:
  //   EJERCICIO 5 - Componente medio compartido
endmodule

module EJ6___Mov_Registros (
  input  Force_input,
  input  en_force_input,
  input  w0,
  input  en0,
  input  w1,
  input  en1,
  input  w2,
  input  en2,
  input  clk,
  output BUS
);

  wire registro_salida_restringida_1_out_debug, registro_salida_restringida_2_out_debug,
       registro_salida_restringida_3_out_debug;

  assign BUS = en_force_input ? Force_input : 1'bz;  // Controlled_Buffer controlled_buffer_1
  registro_salida_restringida registro_salida_restringida_1 (
    .clk(clk), .in(BUS), .out_debug(registro_salida_restringida_1_out_debug), .out(BUS), .w(w0), .en_out(en0));
  // Probe on registro_salida_restringida_1_out_debug
  registro_salida_restringida registro_salida_restringida_2 (
    .clk(clk), .in(BUS), .out_debug(registro_salida_restringida_2_out_debug), .out(BUS), .w(w1), .en_out(en1));
  // Probe on registro_salida_restringida_2_out_debug
  registro_salida_restringida registro_salida_restringida_3 (
    .clk(clk), .in(BUS), .out_debug(registro_salida_restringida_3_out_debug), .out(BUS), .w(w2), .en_out(en2));
  // Probe on registro_salida_restringida_3_out_debug

  // Notes on the sheet:
  //   EJERCICIO 6 - Movimientos entre registros
endmodule

module EJ7___Maquina_4bits (
  input  wA,
  input  en0,
  input  enS,
  input  w0,
  input  wB,
  input  en1,
  input  [1:0] op,
  input  w1,
  input  en2,
  input  w2,
  input  en3,
  input  [3:0] Force_input,
  input  w3,
  input  clk,
  input  en_force_input,
  output V,
  output N,
  output C,
  output Z
);

  wire button_1_out, clk_t, not_1_out;
  wire [3:0] A, A_out, B, B_out, ej4_alu_1_s, R0_out, R0_out4_d, R1_out4_d, R2_out4_d, R3_out4_d, S;

  Hex_Digit_Display hex_digit_display_1 (.value(R0_out4_d));  // open: dp
  registro_4b_salida_restringida R0 (
    .In_4(R0_out), .clk(clk_t), .w(w0), .en_out(en0), .out4_d(R0_out4_d), .out(R0_out));
  Hex_Digit_Display hex_digit_display_2 (.value(R1_out4_d));  // open: dp
  registro_4b_salida_restringida R1 (
    .In_4(R0_out), .clk(clk_t), .w(w1), .en_out(en1), .out4_d(R1_out4_d), .out(R0_out));
  Hex_Digit_Display hex_digit_display_3 (.value(R2_out4_d));  // open: dp
  registro_4b_salida_restringida R2 (
    .In_4(R0_out), .clk(clk_t), .w(w2), .en_out(en2), .out4_d(R2_out4_d), .out(R0_out));
  Hex_Digit_Display hex_digit_display_4 (.value(R3_out4_d));  // open: dp
  registro_4b_salida_restringida R3 (
    .In_4(R0_out), .clk(clk_t), .w(w3), .en_out(en3), .out4_d(R3_out4_d), .out(R0_out));
  Hex_Digit_Display hex_digit_display_5 (.value(Force_input));  // open: dp
  assign R0_out = en_force_input ? Force_input : 4'bz;  // Controlled_Buffer controlled_buffer_1
  Hex_Digit_Display hex_digit_display_6 (.value(R0_out));  // open: dp
  registro_4b_salida_restringida u_A (.In_4(R0_out), .clk(clk_t), .w(wA), .en_out(1'b1), .out4_d(A), .out(A_out));
  registro_4b_salida_restringida u_B (.In_4(R0_out), .clk(clk_t), .w(wB), .en_out(1'b1), .out4_d(B), .out(B_out));
  Button button_1 (.out(button_1_out));
  Hex_Digit_Display hex_digit_display_7 (.value(A));  // open: dp
  or or_1 (clk_t, button_1_out, clk);
  Hex_Digit_Display hex_digit_display_8 (.value(B));  // open: dp
  EJ4___ALU ej4_alu_1 (.OP(op), .A(A_out), .B(B_out), .V(V), .N(N), .C(C), .Z(Z), .S(ej4_alu_1_s));
  not not_1 (not_1_out, clk_t);
  Hex_Digit_Display hex_digit_display_9 (.value(S));  // open: dp
  registro_4b_salida_restringida u_S (
    .In_4(ej4_alu_1_s), .clk(not_1_out), .w(1'b1), .en_out(enS), .out4_d(S), .out(R0_out));

  // Notes on the sheet:
  //   EJERCICIO 7 - Máquina de 4 bits
  //   BUS
  //   =
endmodule

module registro_salida_restringida (
  input  clk,
  input  in,
  input  w,
  input  en_out,
  output out_debug,
  output out
);

  D_Flip_Flop d_ff_1 (.clk(clk), .D(in), .Q(out_debug), .en(w));  // open: Qn, preset, reset
  assign out = en_out ? out_debug : 1'bz;  // Controlled_Buffer controlled_buffer_1

  // Notes on the sheet:
  //   Registro 1b salida restringida
endmodule

module registro_4b_salida_restringida (
  input  [3:0] In_4,
  input  clk,
  input  w,
  input  en_out,
  output [3:0] out4_d,
  output [3:0] out
);

  registro_salida_restringida registro_salida_restringida_1 (
    .clk(clk), .in(In_4[0]), .out_debug(out4_d[0]), .out(out[0]), .w(w), .en_out(en_out));
  registro_salida_restringida registro_salida_restringida_2 (
    .clk(clk), .in(In_4[1]), .out_debug(out4_d[1]), .out(out[1]), .w(w), .en_out(en_out));
  registro_salida_restringida registro_salida_restringida_3 (
    .clk(clk), .in(In_4[2]), .out_debug(out4_d[2]), .out(out[2]), .w(w), .en_out(en_out));
  registro_salida_restringida registro_salida_restringida_4 (
    .clk(clk), .in(In_4[3]), .out_debug(out4_d[3]), .out(out[3]), .w(w), .en_out(en_out));

  // Notes on the sheet:
  //   Registro 4b salida restringida
endmodule
